// Logisim project try.circ as structural Verilog: 1 circuit, main circuit main
module main (
  input  in_1,
  output [15:0] out_2,
  output [11:0] out_3,
  output [15:0] out_4,
  output [2:0] out_5,
  output [15:0] out_6,
  output [2:0] out_7,
  output [2:0] out_8,
  output [2:0] out_9,
  output [15:0] out_10,
  output [3:0] out_11,
  output [5:0] out_12,
  output [15:0] out_13,
  output [11:0] out_14,
  output [15:0] out_15,
  output [15:0] out_16,
  output [15:0] out_17,
  output [15:0] out_18,
  output [15:0] out_19,
  output [15:0] out_20,
  output [15:0] out_21
);

  wire ALUOp, ALUSrc, Branch, clock_1_out, Great_F, JAL, JALR, JR, Jump, Less_F, LUI, MemRead, MemtoReg,
       MemWrite, RegDst, RegWrite, T0, T1, T2, Z_F;
  wire [15:0] bit_extender_1_out, main_4_out_8, Mem;

  control_unit_main main_1 (
    .in_1(out_11), .\function (out_3[2:0]), .LUI(LUI), .R0(T0), .R1(T1), .R2(T2), .Branch(Branch), .Z_F(Z_F),
    .Great_F(Great_F), .Less_F(Less_F), .RegWrite(RegWrite), .RegDst(RegDst), .MemRead(MemRead),
    .MemtoReg(MemtoReg), .MemWrite(MemWrite), .ALUOp(ALUOp), .ALUSrc(ALUSrc), .Jump(Jump), .JR(JR),
    .JALR(JALR), .JAL(JAL), .Rt(out_3[8:6]));
  PC_counter_main main_2 (
    .Imm12(out_3), .Regester(out_4), .Imm6(out_3[5:0]), .JAL(JAL), .JR(JR), .JALR(JALR), .Branch(Branch),
    .out_11(out_14), .CLK(clock_1_out), .Reset(in_1), .J(Jump));
  Clock clock_1 (.out(clock_1_out));
  ROM #(.addrWidth(12), .dataWidth(16)) rom_1 (.addr(out_14), .data({out_11, out_3}));  // open: sel
  RegFile_Decoder_main main_3 (
    .Rs(out_3[11:9]), .Rt(out_3[8:6]), .Rd(out_3[5:3]), .ALU(out_2), .Mem(Mem), .PC(out_14), .Imm(out_3),
    .Rd_2(out_5), .data(out_10), .JALR(JAL), .LUI(LUI), .RegDst(RegDst), .JALR_2(JALR), .MemtoReg(MemtoReg));
  assign bit_extender_1_out = {{10{1'b0}}, out_3[5:0]};  // Bit_Extender bit_extender_1
  Regster_File_main main_4 (
    .Write_Register(out_5), .Read_Register1(out_3[11:9]), .in_3(out_3[8:6]), .in_4(out_10), .out_7(out_4),
    .out_8(main_4_out_8), .in_5(RegWrite), .clock(clock_1_out), .out_9(out_13), .out_10(out_15),
    .out_11(out_16), .out_12(out_17), .out_13(out_18), .out_14(out_19), .out_15(out_20), .out_16(out_21));
  Multiplexer #(.width(16)) multiplexer_1 (
    .in0(main_4_out_8), .in1(bit_extender_1_out), .out(out_6), .sel(ALUSrc));  // open: en
  // FULL_ALU0__1__main main_5: pin names not known; wires that end beside it: T2, Less_F, T1, Great_F, T0, Z_F, out_2
  RAM #(.addrWidth(16), .dataWidth(16), .bus("separate")) ram_1 (
    .addr(out_2), .din(main_4_out_8), .data(Mem), .str(MemWrite), .sel(1'b1), .clk(clock_1_out), .clr(MemRead));  // open: ld

  assign out_7 = out_3[5:3];
  assign out_8 = out_3[8:6];
  assign out_9 = out_3[11:9];
  assign out_12 = out_3[5:0];

  // Other names for the same wires on the sheet: fun[2:0] = out_3[2:0]; Imm6[5:0] = out_3[5:0]; Imm12[11:0] = out_3;
  //   Rd[2:0] = out_3[5:3]; Rt[2:0] = out_3[8:6]; Rs[2:0] = out_3[11:9]; op[3:0] = out_11; A1 = out_11[2];
  //   A0 = out_11[3]; pc[11:0] = out_14; R0[15:0] = out_13; R1[15:0] = out_15; R2[15:0] = out_16; R3[15:0] = out_17;
  //   R4[15:0] = out_18; R5[15:0] = out_19; R6[15:0] = out_20; R7[15:0] = out_21; Rs_pc[15:0] = out_4

  // Notes on the sheet:
  //   contents of rom_1 (hex, n*v repeats v):
  //   a384 0 8354 0 35b 0 2040 0 2081 0 20c2 0 890a 0 1921 0 1520 0 14f2 0 4c02 0 1290 0 403b 0 3800 0
  //   b003 0 55c 0 1b68 0 4e9 0 2040 0 2285 0 22c6 0 4e0 0 3840 0 104e
endmodule
